# Fritzing sketch anemometro_arduino_wifi_mqtt_SolidState (saved by Fritzing 0.9.10b)

parts:
  WeMos_D1_Mini2 = WeMos D1 Mini
  12V_Battery = Lilypad Battery Connect  # not connected
  M1 = Adafruit Anemometer [package=THT]

nets:
  N1: WeMos_D1_Mini2.A0, M1.pin3

custom parts:
  Adafruit Anemometer: Adafruit Anemometer Wind Speed Sensor w/Analog Voltage Output.
